# Fritzing sketch clock_with_ir_led (saved by Fritzing 0.9.3b)
breadboards: 1

parts:
  Arduino_Nano = Arduino Nano (Rev3.0)
  NPN-Transistor = NPN-Transistor [package="TO92 [THT]"]
  Infrared_LED = LED - 5mm [color="Infrared (850nm)" package="5 mm [THT]"]
  DS3231_RTC = ZS-042 RTC Module
  Digit_Display = Grove 4 Digit Display
  Power_Jack = Power Jack [package=power_jack_smd]

nets:
  GND: Arduino_Nano.GND, Infrared_LED.cathode, DS3231_RTC.GND, Digit_Display.GND, Power_Jack.GND
  N1: Arduino_Nano.D3, NPN-Transistor.B
  N2: Arduino_Nano.D7, Digit_Display.DIO
  N3: Arduino_Nano.D8, Digit_Display.CLK
  N4: Arduino_Nano.VIN, Power_Jack.GNDBREAK
  VCC: Arduino_Nano.5V, NPN-Transistor.C, DS3231_RTC.VCC, Digit_Display.VCC
  N5: Arduino_Nano.A5, DS3231_RTC.SCL
  N6: Arduino_Nano.A4, DS3231_RTC.SDA
  N7: NPN-Transistor.E, Infrared_LED.anode
